# Fritzing sketch ClydeWinterSchematic (saved by Fritzing 0.9.1b)
breadboards: 1

parts:
  LED1 = LED - 5mm [color="White (4500K)" package="5 mm [THT]"]
  U1 = 74HC595 [package="DIP16 [THT]"]
  C1 = Ceramic Capacitor [capacitance=0.1µF package="100 mil [THT, multilayer]"]
  R2 = Resistor [tolerance=±5% resistance=220 package=THT]
  R3 = Resistor [tolerance=±5% resistance=220 package=THT]
  R4 = Resistor [tolerance=±5% resistance=220 package=THT]
  R5 = Resistor [tolerance=±5% resistance=220 package=THT]
  R6 = Resistor [tolerance=±5% resistance=220 package=THT]
  R7 = Resistor [tolerance=±5% resistance=220 package=THT]
  R8 = Resistor [tolerance=±5% resistance=220 package=THT]
  R9 = Resistor [tolerance=±5% resistance=220 package=THT]
  LED3 = LED - 5mm [color="White (4500K)" package="5 mm [THT]"]
  LED4 = LED - 5mm [color="White (4500K)" package="5 mm [THT]"]
  LED5 = LED - 5mm [color="White (4500K)" package="5 mm [THT]"]
  LED6 = LED - 5mm [color="White (4500K)" package="5 mm [THT]"]
  LED7 = LED - 5mm [color="White (4500K)" package="5 mm [THT]"]
  LED8 = LED - 5mm [color="White (4500K)" package="5 mm [THT]"]
  LED9 = LED - 5mm [color="White (4500K)" package="5 mm [THT]"]

nets:
  N1: LED1.anode, R8.Pin_1
  N2: U1.Q1, R2.Pin_0
  N3: U1.Q2, R3.Pin_0
  N4: U1.Q3, R4.Pin_0
  N5: U1.Q4, R5.Pin_0
  N6: U1.Q5, R6.Pin_0
  N7: U1.Q6, R7.Pin_0
  N8: U1.Q7, R8.Pin_0
  N9: U1.ST_CP, C1.1
  N10: U1.OE, C1.0
  N11: U1.Q0, R9.Pin_0
  N12: R2.Pin_1, LED9.anode
  N13: R3.Pin_1, LED8.anode
  N14: R4.Pin_1, LED7.anode
  N15: R5.Pin_1, LED6.anode
  N16: R6.Pin_1, LED5.anode
  N17: R7.Pin_1, LED4.anode
  N18: R9.Pin_1, LED3.anode

notes:
  ST_CP -> 10
  DS -> 13
  SH_CP -> 12
